# Fritzing sketch MA6 (saved by Fritzing 1.0.4)
breadboards: 3

parts:
  LED1 = LED - 5mm [color="Red (633nm)" current=0.030A package="5 mm [THT]"]
  R1 = Resistor [tolerance=±5% power=0.25W resistance=220 package=THT]
  VCC1 = 4 x AAA Battery Mount [internal_resistance=0.1Ω]
  VM1 = Multimeter (DC Voltage)
  M2 = DC Motor [voltage_(max)=6V voltage_(min)=3V]
  VCC2 = 4 x AAA Battery Mount [internal_resistance=0.1Ω]
  S2 = Pushbutton [package=THT]
  S3 = Pushbutton [package=THT]
  S1 = Pushbutton [package=THT]
  S4 = Pushbutton [package=THT]
  M3 = DC Motor [voltage_(max)=6V voltage_(min)=3V]
  VCC3 = 4 x AAA Battery Mount [internal_resistance=0.1Ω]
  Q1 = NPN-Transistor [package="TO92 [THT]"]
  R2 = Resistor [tolerance=±5% power=0.25W resistance=150 package=THT]
  M4 = fc-51 [package=THT]
  M1 = fc-51 [package=THT]

nets:
  GND: LED1.cathode, VCC1.-, VM1.COM_Probe, VCC2.-, S3.leg0, S4.leg0, VCC3.-, Q1.E, M4.pin2, M1.pin2
  N1: LED1.anode, R1.Pin_0
  ir_out: R1.Pin_1, VM1.V_Probe, M1.pin1
  5V: VCC1.+, VCC2.+, S2.leg1, S1.leg1, M3.pin_1, VCC3.+, M4.pin3, M1.pin3
  N2: M2.pin_1, S2.leg0, S4.leg1
  N3: M2.pin_2, S3.leg1, S1.leg0
  N4: M3.pin_2, Q1.C
  N5: Q1.B, R2.Pin_1
  N6: R2.Pin_0, M4.pin1
